// Logisim project 8bitcalc.circ as structural Verilog: 11 circuits, main circuit main
module main (
  input  a7,
  input  a6,
  input  a5,
  input  a4,
  input  a3,
  input  a2,
  input  a1,
  input  a0,
  input  b7,
  input  b6,
  input  b5,
  input  b4,
  input  b3,
  input  b2,
  input  b1,
  input  b0,
  input  in_17,
  input  in_18,
  input  Q_R
);

  wire adder_subtractor_8_bit_1_out_24, adder_subtractor_8_bit_1_s0, adder_subtractor_8_bit_1_s1,
       adder_subtractor_8_bit_1_s2, adder_subtractor_8_bit_1_s3, adder_subtractor_8_bit_1_s4,
       adder_subtractor_8_bit_1_s5, adder_subtractor_8_bit_1_s6, adder_subtractor_8_bit_1_s7,
       adder_subtractor_8_bit_1_s8, demultiplexer_1_out2, demultiplexer_1_out3, dividor8bit_1_lsb,
       dividor8bit_1_out_17, dividor8bit_1_out_22, dividor8bit_1_out_23, dividor8bit_1_out_24,
       dividor8bit_1_out_25, dividor8bit_1_out_26, dividor8bit_1_out_27, dividor8bit_1_out_28,
       dividor8bit_1_out_29, dividor8bit_1_q3, dividor8bit_1_q4, dividor8bit_1_q5, dividor8bit_1_q6,
       dividor8bit_1_r1, dividor8bit_1_r2, hexato7segment_1_a, hexato7segment_1_b, hexato7segment_1_c,
       hexato7segment_1_d, hexato7segment_1_e, hexato7segment_1_f, hexato7segment_1_g, hexato7segment_2_a,
       hexato7segment_2_b, hexato7segment_2_c, hexato7segment_2_d, hexato7segment_2_e, hexato7segment_2_f,
       hexato7segment_2_g, hexato7segment_3_a, hexato7segment_3_b, hexato7segment_3_c, hexato7segment_3_d,
       hexato7segment_3_e, hexato7segment_3_f, hexato7segment_3_g, hexato7segment_4_a, hexato7segment_4_b,
       hexato7segment_4_c, hexato7segment_4_d, hexato7segment_4_e, hexato7segment_4_f, hexato7segment_4_g,
       multiplexer_1_out, n8_bitmultiplier_1_m0, n8_bitmultiplier_1_m1, n8_bitmultiplier_1_m2,
       n8_bitmultiplier_1_m3, n8_bitmultiplier_1_m4_prime, n8_bitmultiplier_1_m5, n8_bitmultiplier_1_m6,
       n8_bitmultiplier_1_m7, n8_bitmultiplier_1_m8, n8_bitmultiplier_1_m9, n8_bitmultiplier_1_m10,
       n8_bitmultiplier_1_m11, n8_bitmultiplier_1_m12, n8_bitmultiplier_1_m13, n8_bitmultiplier_1_m14,
       n8_bitmultiplier_1_m15, n9andgates_1_out_11, n9andgates_1_out_12, n9andgates_1_out_13,
       n9andgates_1_out_14, n9andgates_1_out_15, n9andgates_1_out_16, n9andgates_1_out_17,
       n9andgates_1_out_18, n9andgates_2_out_11, n9andgates_2_out_12, n9andgates_2_out_13,
       n9andgates_2_out_14, n9andgates_2_out_15, n9andgates_2_out_16, n9andgates_2_out_17,
       n9andgates_2_out_18, n9andgates_3_out_11, n9andgates_3_out_12, n9andgates_3_out_13,
       n9andgates_3_out_14, n9andgates_3_out_15, n9andgates_3_out_16, n9andgates_3_out_17,
       n9andgates_3_out_18, n9andgates_4_out_11, n9andgates_4_out_12, n9andgates_4_out_13,
       n9andgates_4_out_14, n9andgates_4_out_15, n9andgates_4_out_16, n9andgates_4_out_17,
       n9andgates_4_out_18, n9andgates_4_out_19, n16orgates_1_out_33, n16orgates_1_out_34,
       n16orgates_1_out_35, n16orgates_1_out_36, n16orgates_1_out_37, n16orgates_1_out_38,
       n16orgates_1_out_39, n16orgates_1_out_40, n16orgates_1_out_41, n16orgates_1_out_42,
       n16orgates_1_out_43, n16orgates_1_out_44, n16orgates_1_out_45, n16orgates_1_out_46,
       n16orgates_1_out_47, n16orgates_1_out_48, n16orgates_2_out_33, n16orgates_2_out_34,
       n16orgates_2_out_35, n16orgates_2_out_36, n16orgates_2_out_37, n16orgates_2_out_38,
       n16orgates_2_out_39, n16orgates_2_out_40, n16orgates_2_out_41, n16orgates_2_out_42,
       n16orgates_2_out_43, n16orgates_2_out_44, n16orgates_2_out_45, n16orgates_2_out_46,
       n16orgates_2_out_47, n16orgates_2_out_48, n16orgates_3_out_33, n16orgates_3_out_34,
       n16orgates_3_out_35, n16orgates_3_out_36, n16orgates_3_out_37, n16orgates_3_out_38,
       n16orgates_3_out_39, n16orgates_3_out_40, n16orgates_3_out_41, n16orgates_3_out_42,
       n16orgates_3_out_43, n16orgates_3_out_44, n16orgates_3_out_45, n16orgates_3_out_46,
       n16orgates_3_out_47, n16orgates_3_out_48, not_1_out, not_2_out, not_3_out;

  Demultiplexer #(.select(2)) demultiplexer_1 (
    .out2(demultiplexer_1_out2), .out3(demultiplexer_1_out3), .in(1'b1), .sel({in_17, in_18}), .en(1'b1));  // open: out0, out1
  not not_1 (not_1_out, 1'b0);
  Multiplexer #(.select(2)) multiplexer_1 (
    .in0(1'b0), .in1(1'b0), .in2(not_1_out), .in3(1'b0), .out(multiplexer_1_out), .sel({in_18, in_17}),
    .en(1'b1));
  _8_BitMultiplier u_8_bitmultiplier_1 (
    .Zero(1'b0), .a7(a7), .a6(a6), .a5(a5), .a4(a4), .a3(a3), .a2(a2), .a1(a1), .a0(a0),
    .m0(n8_bitmultiplier_1_m0), .m1(n8_bitmultiplier_1_m1), .m2(n8_bitmultiplier_1_m2),
    .m3(n8_bitmultiplier_1_m3), .m4_prime(n8_bitmultiplier_1_m4_prime), .m5(n8_bitmultiplier_1_m5), .b7(b7),
    .b6(b6), .b5(b5), .b4(b4), .b3(b3), .b2(b2), .b1(b1), .b0(b0), .m6(n8_bitmultiplier_1_m6),
    .EN(demultiplexer_1_out2), .m7(n8_bitmultiplier_1_m7), .m8(n8_bitmultiplier_1_m8),
    .m9(n8_bitmultiplier_1_m9), .m10(n8_bitmultiplier_1_m10), .m11(n8_bitmultiplier_1_m11),
    .m12(n8_bitmultiplier_1_m12), .m13(n8_bitmultiplier_1_m13), .m14(n8_bitmultiplier_1_m14),
    .m15(n8_bitmultiplier_1_m15));
  dividor8bit dividor8bit_1 (
    .q6(dividor8bit_1_q6), .q5(dividor8bit_1_q5), .q4(dividor8bit_1_q4), .q3(dividor8bit_1_q3),
    .out_22(dividor8bit_1_out_22), .out_24(dividor8bit_1_out_24), .a7(a7), .a6(a6), .a5(a5), .a4(a4),
    .a3(a3), .a2(a2), .a1(a1), .a0(a0), .b7(b7), .b6(b6), .b5(b5), .b4(b4), .b3(b3), .b2(b2), .b1(b1),
    .b0(b0), .out_25(dividor8bit_1_out_25), .out_26(dividor8bit_1_out_26), .out_27(dividor8bit_1_out_27),
    .out_28(dividor8bit_1_out_28), .out_29(dividor8bit_1_out_29), .r2(dividor8bit_1_r2),
    .r1(dividor8bit_1_r1), .LSB(dividor8bit_1_lsb), .out_23(dividor8bit_1_out_23),
    .out_17(dividor8bit_1_out_17));
  _9andgates u_9andgates_1 (
    .EN(demultiplexer_1_out3), .a0(dividor8bit_1_out_24), .a1(dividor8bit_1_out_23),
    .a2(dividor8bit_1_out_22), .a3(dividor8bit_1_q3), .a4(dividor8bit_1_q4), .a5(dividor8bit_1_q5),
    .a6(dividor8bit_1_q6), .a7(dividor8bit_1_out_17), .out_11(n9andgates_1_out_11),
    .out_12(n9andgates_1_out_12), .out_13(n9andgates_1_out_13), .out_14(n9andgates_1_out_14),
    .out_15(n9andgates_1_out_15), .out_16(n9andgates_1_out_16), .out_17(n9andgates_1_out_17),
    .out_18(n9andgates_1_out_18));  // open: a8, out_19
  _9andgates u_9andgates_2 (
    .EN(Q_R), .a0(dividor8bit_1_lsb), .a1(dividor8bit_1_r1), .a2(dividor8bit_1_r2),
    .a3(dividor8bit_1_out_29), .a4(dividor8bit_1_out_28), .a5(dividor8bit_1_out_27),
    .a6(dividor8bit_1_out_26), .a7(dividor8bit_1_out_25), .out_11(n9andgates_2_out_11),
    .out_12(n9andgates_2_out_12), .out_13(n9andgates_2_out_13), .out_14(n9andgates_2_out_14),
    .out_15(n9andgates_2_out_15), .out_16(n9andgates_2_out_16), .out_17(n9andgates_2_out_17),
    .out_18(n9andgates_2_out_18));  // open: a8, out_19
  Adder_Subtractor_8_Bit adder_subtractor_8_bit_1 (
    .a7(a7), .a6(a6), .a5(a5), .a4(a4), .a3(a3), .a2(a2), .a1(a1), .a0(a0), .a7_2(b7), .a6_2(b6), .a5_2(b5),
    .a4_2(b4), .a3_2(b3), .a2_2(b2), .a1_2(b1), .a0_2(b0), .M(multiplexer_1_out),
    .s0(adder_subtractor_8_bit_1_s0), .s1(adder_subtractor_8_bit_1_s1), .s2(adder_subtractor_8_bit_1_s2),
    .s3(adder_subtractor_8_bit_1_s3), .s4(adder_subtractor_8_bit_1_s4), .s5(adder_subtractor_8_bit_1_s5),
    .s6(adder_subtractor_8_bit_1_s6), .s7(adder_subtractor_8_bit_1_s7), .s8(adder_subtractor_8_bit_1_s8),
    .O(1'b1), .out_24(adder_subtractor_8_bit_1_out_24));
  not not_2 (not_2_out, Q_R);
  _9andgates u_9andgates_3 (
    .EN(not_2_out), .a0(n9andgates_1_out_11), .a1(n9andgates_1_out_12), .a2(n9andgates_1_out_13),
    .a3(n9andgates_1_out_14), .a4(n9andgates_1_out_15), .a5(n9andgates_1_out_16), .a6(n9andgates_1_out_17),
    .a7(n9andgates_1_out_18), .out_11(n9andgates_3_out_11), .out_12(n9andgates_3_out_12),
    .out_13(n9andgates_3_out_13), .out_14(n9andgates_3_out_14), .out_15(n9andgates_3_out_15),
    .out_16(n9andgates_3_out_16), .out_17(n9andgates_3_out_17), .out_18(n9andgates_3_out_18));  // open: a8, out_19
  not not_3 (not_3_out, in_17);
  _16orgates u_16orgates_1 (
    .out_33(n16orgates_1_out_33), .a0(n9andgates_3_out_11), .b0(n9andgates_2_out_11),
    .a0_2(n9andgates_3_out_12), .out_34(n16orgates_1_out_34), .b0_2(n9andgates_2_out_12),
    .a0_3(n9andgates_3_out_13), .out_35(n16orgates_1_out_35), .b0_3(n9andgates_2_out_13),
    .a0_4(n9andgates_3_out_14), .out_36(n16orgates_1_out_36), .b0_4(n9andgates_2_out_14),
    .a0_5(n9andgates_3_out_15), .out_37(n16orgates_1_out_37), .b0_5(n9andgates_2_out_15),
    .a0_6(n9andgates_3_out_16), .out_38(n16orgates_1_out_38), .b0_6(n9andgates_2_out_16),
    .a0_7(n9andgates_3_out_17), .out_39(n16orgates_1_out_39), .b0_7(n9andgates_2_out_17),
    .a0_8(n9andgates_3_out_18), .out_40(n16orgates_1_out_40), .b0_8(n9andgates_2_out_18), .a0_9(1'b0),
    .out_41(n16orgates_1_out_41), .b0_9(1'b0), .a0_10(1'b0), .out_42(n16orgates_1_out_42), .b0_10(1'b0),
    .a0_11(1'b0), .out_43(n16orgates_1_out_43), .b0_11(1'b0), .a0_12(1'b0), .out_44(n16orgates_1_out_44),
    .b0_12(1'b0), .a0_13(1'b0), .out_45(n16orgates_1_out_45), .b0_13(1'b0), .a0_14(1'b0),
    .out_46(n16orgates_1_out_46), .b0_14(1'b0), .a0_15(1'b0), .out_47(n16orgates_1_out_47), .b0_15(1'b0),
    .a0_16(1'b0), .out_48(n16orgates_1_out_48), .b0_16(1'b0));
  _9andgates u_9andgates_4 (
    .EN(not_3_out), .a0(adder_subtractor_8_bit_1_s0), .a1(adder_subtractor_8_bit_1_s1),
    .a2(adder_subtractor_8_bit_1_s2), .a3(adder_subtractor_8_bit_1_s3), .a4(adder_subtractor_8_bit_1_s4),
    .a5(adder_subtractor_8_bit_1_s5), .a6(adder_subtractor_8_bit_1_s6), .a7(adder_subtractor_8_bit_1_s7),
    .a8(adder_subtractor_8_bit_1_s8), .out_11(n9andgates_4_out_11), .out_12(n9andgates_4_out_12),
    .out_13(n9andgates_4_out_13), .out_14(n9andgates_4_out_14), .out_15(n9andgates_4_out_15),
    .out_16(n9andgates_4_out_16), .out_17(n9andgates_4_out_17), .out_18(n9andgates_4_out_18),
    .out_19(n9andgates_4_out_19));
  _16orgates u_16orgates_2 (
    .out_33(n16orgates_2_out_33), .a0(n9andgates_4_out_11), .b0(n8_bitmultiplier_1_m0),
    .a0_2(n9andgates_4_out_12), .out_34(n16orgates_2_out_34), .b0_2(n8_bitmultiplier_1_m1),
    .a0_3(n9andgates_4_out_13), .out_35(n16orgates_2_out_35), .b0_3(n8_bitmultiplier_1_m2),
    .a0_4(n9andgates_4_out_14), .out_36(n16orgates_2_out_36), .b0_4(n8_bitmultiplier_1_m3),
    .a0_5(n9andgates_4_out_15), .out_37(n16orgates_2_out_37), .b0_5(n8_bitmultiplier_1_m4_prime),
    .a0_6(n9andgates_4_out_16), .out_38(n16orgates_2_out_38), .b0_6(n8_bitmultiplier_1_m5),
    .a0_7(n9andgates_4_out_17), .out_39(n16orgates_2_out_39), .b0_7(n8_bitmultiplier_1_m6),
    .a0_8(n9andgates_4_out_18), .out_40(n16orgates_2_out_40), .b0_8(n8_bitmultiplier_1_m7),
    .a0_9(n9andgates_4_out_19), .out_41(n16orgates_2_out_41), .b0_9(n8_bitmultiplier_1_m8), .a0_10(1'b0),
    .out_42(n16orgates_2_out_42), .b0_10(n8_bitmultiplier_1_m9), .a0_11(1'b0), .out_43(n16orgates_2_out_43),
    .b0_11(n8_bitmultiplier_1_m10), .a0_12(1'b0), .out_44(n16orgates_2_out_44),
    .b0_12(n8_bitmultiplier_1_m11), .a0_13(1'b0), .out_45(n16orgates_2_out_45),
    .b0_13(n8_bitmultiplier_1_m12), .a0_14(1'b0), .out_46(n16orgates_2_out_46),
    .b0_14(n8_bitmultiplier_1_m13), .a0_15(1'b0), .out_47(n16orgates_2_out_47),
    .b0_15(n8_bitmultiplier_1_m14), .a0_16(1'b0), .out_48(n16orgates_2_out_48), .b0_16(n8_bitmultiplier_1_m15));
  _16orgates u_16orgates_3 (
    .out_33(n16orgates_3_out_33), .a0(n16orgates_2_out_33), .b0(n16orgates_1_out_33),
    .a0_2(n16orgates_2_out_34), .out_34(n16orgates_3_out_34), .b0_2(n16orgates_1_out_34),
    .a0_3(n16orgates_2_out_35), .out_35(n16orgates_3_out_35), .b0_3(n16orgates_1_out_35),
    .a0_4(n16orgates_2_out_36), .out_36(n16orgates_3_out_36), .b0_4(n16orgates_1_out_36),
    .a0_5(n16orgates_2_out_37), .out_37(n16orgates_3_out_37), .b0_5(n16orgates_1_out_37),
    .a0_6(n16orgates_2_out_38), .out_38(n16orgates_3_out_38), .b0_6(n16orgates_1_out_38),
    .a0_7(n16orgates_2_out_39), .out_39(n16orgates_3_out_39), .b0_7(n16orgates_1_out_39),
    .a0_8(n16orgates_2_out_40), .out_40(n16orgates_3_out_40), .b0_8(n16orgates_1_out_40),
    .a0_9(n16orgates_2_out_41), .out_41(n16orgates_3_out_41), .b0_9(n16orgates_1_out_41),
    .a0_10(n16orgates_2_out_42), .out_42(n16orgates_3_out_42), .b0_10(n16orgates_1_out_42),
    .a0_11(n16orgates_2_out_43), .out_43(n16orgates_3_out_43), .b0_11(n16orgates_1_out_43),
    .a0_12(n16orgates_2_out_44), .out_44(n16orgates_3_out_44), .b0_12(n16orgates_1_out_44),
    .a0_13(n16orgates_2_out_45), .out_45(n16orgates_3_out_45), .b0_13(n16orgates_1_out_45),
    .a0_14(n16orgates_2_out_46), .out_46(n16orgates_3_out_46), .b0_14(n16orgates_1_out_46),
    .a0_15(n16orgates_2_out_47), .out_47(n16orgates_3_out_47), .b0_15(n16orgates_1_out_47),
    .a0_16(n16orgates_2_out_48), .out_48(n16orgates_3_out_48), .b0_16(n16orgates_1_out_48));
  hexato7segment hexato7segment_1 (
    .a0(n16orgates_3_out_45), .a1(n16orgates_3_out_46), .a2(n16orgates_3_out_47), .a3(n16orgates_3_out_48),
    .a(hexato7segment_1_a), .b(hexato7segment_1_b), .c(hexato7segment_1_c), .d(hexato7segment_1_d),
    .e(hexato7segment_1_e), .f(hexato7segment_1_f), .g(hexato7segment_1_g));
  _7_Segment_Display u_7_segment_display_1 (.g(adder_subtractor_8_bit_1_out_24));  // open: f, a, b, e, d, c, dp
  hexato7segment hexato7segment_2 (
    .a0(n16orgates_3_out_41), .a1(n16orgates_3_out_42), .a2(n16orgates_3_out_43), .a3(n16orgates_3_out_44),
    .a(hexato7segment_2_a), .b(hexato7segment_2_b), .c(hexato7segment_2_c), .d(hexato7segment_2_d),
    .e(hexato7segment_2_e), .f(hexato7segment_2_f), .g(hexato7segment_2_g));
  _7_Segment_Display u_7_segment_display_2 (
    .g(hexato7segment_1_g), .f(hexato7segment_1_e), .a(hexato7segment_1_f), .b(hexato7segment_1_a),
    .e(hexato7segment_1_d), .d(hexato7segment_1_c), .c(hexato7segment_1_b));  // open: dp
  hexato7segment hexato7segment_3 (
    .a0(n16orgates_3_out_37), .a1(n16orgates_3_out_38), .a2(n16orgates_3_out_39), .a3(n16orgates_3_out_40),
    .a(hexato7segment_3_a), .b(hexato7segment_3_b), .c(hexato7segment_3_c), .d(hexato7segment_3_d),
    .e(hexato7segment_3_e), .f(hexato7segment_3_f), .g(hexato7segment_3_g));
  _7_Segment_Display u_7_segment_display_3 (
    .g(hexato7segment_2_g), .f(hexato7segment_2_e), .a(hexato7segment_2_f), .b(hexato7segment_2_a),
    .e(hexato7segment_2_d), .d(hexato7segment_2_c), .c(hexato7segment_2_b));  // open: dp
  _7_Segment_Display u_7_segment_display_4 (
    .g(hexato7segment_3_g), .f(hexato7segment_3_e), .a(hexato7segment_3_f), .b(hexato7segment_3_a),
    .e(hexato7segment_3_d), .d(hexato7segment_3_c), .c(hexato7segment_3_b));  // open: dp
  hexato7segment hexato7segment_4 (
    .a0(n16orgates_3_out_33), .a1(n16orgates_3_out_34), .a2(n16orgates_3_out_35), .a3(n16orgates_3_out_36),
    .a(hexato7segment_4_a), .b(hexato7segment_4_b), .c(hexato7segment_4_c), .d(hexato7segment_4_d),
    .e(hexato7segment_4_e), .f(hexato7segment_4_f), .g(hexato7segment_4_g));
  _7_Segment_Display u_7_segment_display_5 (
    .g(hexato7segment_4_g), .f(hexato7segment_4_e), .a(hexato7segment_4_f), .b(hexato7segment_4_a),
    .e(hexato7segment_4_d), .d(hexato7segment_4_c), .c(hexato7segment_4_b));  // open: dp

  // Notes on the sheet:
  //   A
  //   B
  //   Operations:
  //   Addition: A+B (00)
  //   Subtraction : A-B (01)
  //   Multiplication: A*B (10)
  //   Division: A/B (11)
endmodule

module _8_BitLookAhead (
  input  in_1,
  input  a3,
  input  a2,
  input  a1,
  input  a0,
  input  b3,
  input  b2,
  input  b1,
  input  b0,
  input  a7,
  input  a6,
  input  a5,
  input  a4,
  input  b7,
  input  b6,
  input  b5,
  input  b4,
  output o3,
  output o2,
  output o1,
  output o0,
  output o8,
  output o7,
  output o6,
  output o5,
  output o4
);

  wire and_1_out, and_2_out, and_3_out, and_4_out, and_5_out, and_6_out, and_7_out, and_8_out, and_9_out,
       and_10_out, and_11_out, and_12_out, and_13_out, and_14_out, and_15_out, and_16_out, and_17_out,
       and_18_out, and_19_out, and_20_out, c1_2_out, c1_out, c2_2_out, c2_out, c3_2_out, c3_out, c4_out,
       g0_2_out, g0_out, g1_2_out, g1_out, g2_2_out, g2_out, g3_2_out, g3_out, p0_2_out, p0_out, p1_2_out,
       p1_out, p2_2_out, p2_out, p3_2_out, p3_out;

  and g3 (g3_out, a3, b3);
  and g0 (g0_out, a0, b0);
  xor p1 (p1_out, a1, b1);
  and g1 (g1_out, a1, b1);
  xor p3 (p3_out, a3, b3);
  xor p0 (p0_out, a0, b0);
  xor p2 (p2_out, b2, a2);
  and g2 (g2_out, b2, a2);
  xor p3_2 (p3_2_out, a7, b7);
  and g3_2 (g3_2_out, a7, b7);
  xor s0 (o0, in_1, p0_out);
  and and_1 (and_1_out, p1_out, g0_out);
  and and_2 (and_2_out, p1_out, p0_out, in_1);
  xor p0_2 (p0_2_out, a4, b4);
  and g0_2 (g0_2_out, a4, b4);
  xor p1_2 (p1_2_out, a5, b5);
  and g1_2 (g1_2_out, a5, b5);
  xor p2_2 (p2_2_out, b6, a6);
  and g2_2 (g2_2_out, b6, a6);
  and and_3 (and_3_out, in_1, p0_out);
  and and_4 (and_4_out, p2_out, g1_out);
  and and_5 (and_5_out, p2_out, p1_out, g0_out);
  and and_6 (and_6_out, p2_out, p1_out, p0_out, in_1);
  and and_7 (and_7_out, p3_out, g2_out);
  and and_8 (and_8_out, p3_out, p2_out, g1_out);
  and and_9 (and_9_out, p3_out, p2_out, p1_out, g0_out);
  and and_10 (and_10_out, p3_out, p2_out, p1_out, p0_out, in_1);
  xor s0_2 (o4, c4_out, p0_2_out);
  or c1 (c1_out, and_3_out, g0_out);
  or c2 (c2_out, g1_out, and_1_out, and_2_out);
  or c3 (c3_out, g2_out, and_4_out, and_5_out, and_6_out);
  and and_11 (and_11_out, c4_out, p0_2_out);
  and and_12 (and_12_out, p1_2_out, g0_2_out);
  and and_13 (and_13_out, p1_2_out, p0_2_out, c4_out);
  and and_14 (and_14_out, p2_2_out, g1_2_out);
  and and_15 (and_15_out, p2_2_out, p1_2_out, g0_2_out);
  and and_16 (and_16_out, p2_2_out, p1_2_out, p0_2_out, c4_out);
  and and_17 (and_17_out, p3_2_out, g2_2_out);
  and and_18 (and_18_out, p3_2_out, p2_2_out, g1_2_out);
  and and_19 (and_19_out, p3_2_out, p2_2_out, p1_2_out, g0_2_out);
  and and_20 (and_20_out, p3_2_out, p2_2_out, p1_2_out, p0_2_out, c4_out);
  xor s1 (o1, c1_out, p1_out);
  xor s2 (o2, c2_out, p2_out);
  or c4 (c4_out, g3_out, and_7_out, and_8_out, and_9_out, and_10_out);
  or c1_2 (c1_2_out, and_11_out, g0_2_out);
  or c2_2 (c2_2_out, g1_2_out, and_12_out, and_13_out);
  xor s3 (o3, c3_out, p3_out);
  xor s1_2 (o5, c1_2_out, p1_2_out);
  xor s2_2 (o6, c2_2_out, p2_2_out);
  or c3_2 (c3_2_out, g2_2_out, and_14_out, and_15_out, and_16_out);
  or c4_2 (o8, g3_2_out, and_17_out, and_18_out, and_19_out, and_20_out);
  xor s3_2 (o7, c3_2_out, p3_2_out);
endmodule

module _8_BitMultiplier (
  input  Zero,
  input  a7,
  input  a6,
  input  a5,
  input  a4,
  input  a3,
  input  a2,
  input  a1,
  input  a0,
  input  b7,
  input  b6,
  input  b5,
  input  b4,
  input  b3,
  input  b2,
  input  b1,
  input  b0,
  input  EN,
  output m0,
  output m1,
  output m2,
  output m3,
  output m4_prime,
  output m5,
  output m6,
  output m7,
  output m8,
  output m9,
  output m10,
  output m11,
  output m12,
  output m13,
  output m14,
  output m15
);

  wire and_2_out, and_3_out, and_4_out, and_5_out, and_6_out, and_7_out, and_8_out, and_9_out, and_10_out,
       and_11_out, and_12_out, and_13_out, and_14_out, and_15_out, and_16_out, and_17_out, and_18_out,
       and_19_out, and_20_out, and_21_out, and_22_out, and_23_out, and_24_out, and_25_out, and_26_out,
       and_27_out, and_28_out, and_29_out, and_30_out, and_31_out, and_32_out, and_33_out, and_34_out,
       and_35_out, and_36_out, and_37_out, and_38_out, and_39_out, and_40_out, and_41_out, and_42_out,
       and_43_out, and_44_out, and_45_out, and_46_out, and_47_out, and_48_out, and_49_out, and_50_out,
       and_51_out, and_52_out, and_53_out, and_54_out, and_55_out, and_56_out, and_57_out, and_58_out,
       and_59_out, and_60_out, and_61_out, and_62_out, and_63_out, and_64_out, n8_bitlookahead_1_o1,
       n8_bitlookahead_1_o2, n8_bitlookahead_1_o3, n8_bitlookahead_1_o4, n8_bitlookahead_1_o5,
       n8_bitlookahead_1_o6, n8_bitlookahead_1_o7, n8_bitlookahead_1_o8, n8_bitlookahead_2_o1,
       n8_bitlookahead_2_o2, n8_bitlookahead_2_o3, n8_bitlookahead_2_o4, n8_bitlookahead_2_o5,
       n8_bitlookahead_2_o6, n8_bitlookahead_2_o7, n8_bitlookahead_2_o8, n8_bitlookahead_3_o1,
       n8_bitlookahead_3_o2, n8_bitlookahead_3_o3, n8_bitlookahead_3_o4, n8_bitlookahead_3_o5,
       n8_bitlookahead_3_o6, n8_bitlookahead_3_o7, n8_bitlookahead_3_o8, n8_bitlookahead_4_o1,
       n8_bitlookahead_4_o2, n8_bitlookahead_4_o3, n8_bitlookahead_4_o4, n8_bitlookahead_4_o5,
       n8_bitlookahead_4_o6, n8_bitlookahead_4_o7, n8_bitlookahead_4_o8, n8_bitlookahead_6_o1,
       n8_bitlookahead_6_o2, n8_bitlookahead_6_o3, n8_bitlookahead_6_o4, n8_bitlookahead_6_o5,
       n8_bitlookahead_6_o6, n8_bitlookahead_6_o7, n8_bitlookahead_6_o8, n8_bitlookahead_7_o1,
       n8_bitlookahead_7_o2, n8_bitlookahead_7_o3, n8_bitlookahead_7_o4, n8_bitlookahead_7_o5,
       n8_bitlookahead_7_o6, n8_bitlookahead_7_o7, n8_bitlookahead_7_o8;

  and and_1 (m0, EN, b0, a0);
  and and_2 (and_2_out, EN, b1, a0);
  and and_3 (and_3_out, EN, b2, a0);
  and and_4 (and_4_out, EN, b3, a0);
  and and_5 (and_5_out, EN, b4, a0);
  and and_6 (and_6_out, EN, b5, a0);
  and and_7 (and_7_out, EN, b6, a0);
  and and_8 (and_8_out, EN, b7, a0);
  and and_9 (and_9_out, EN, b0, a1);
  and and_10 (and_10_out, EN, b1, a1);
  and and_11 (and_11_out, EN, b2, a1);
  and and_12 (and_12_out, EN, b3, a1);
  and and_13 (and_13_out, EN, b4, a1);
  and and_14 (and_14_out, EN, b5, a1);
  and and_15 (and_15_out, EN, b6, a1);
  and and_16 (and_16_out, EN, b7, a1);
  and and_17 (and_17_out, EN, b0, a2);
  and and_18 (and_18_out, EN, b1, a2);
  and and_19 (and_19_out, EN, b2, a2);
  and and_20 (and_20_out, EN, b3, a2);
  and and_21 (and_21_out, EN, b4, a2);
  and and_22 (and_22_out, EN, b5, a2);
  and and_23 (and_23_out, EN, b6, a2);
  and and_24 (and_24_out, EN, b7, a2);
  and and_25 (and_25_out, EN, b0, a3);
  and and_26 (and_26_out, EN, b1, a3);
  and and_27 (and_27_out, EN, b2, a3);
  and and_28 (and_28_out, EN, b3, a3);
  and and_29 (and_29_out, EN, b4, a3);
  and and_30 (and_30_out, EN, b5, a3);
  and and_31 (and_31_out, EN, b6, a3);
  and and_32 (and_32_out, EN, b7, a3);
  and and_33 (and_33_out, EN, b0, a4);
  and and_34 (and_34_out, EN, b1, a4);
  and and_35 (and_35_out, EN, b2, a4);
  and and_36 (and_36_out, EN, b3, a4);
  and and_37 (and_37_out, EN, b4, a4);
  and and_38 (and_38_out, EN, b5, a4);
  and and_39 (and_39_out, EN, b6, a4);
  and and_40 (and_40_out, EN, b7, a4);
  and and_41 (and_41_out, EN, b0, a5);
  and and_42 (and_42_out, EN, b1, a5);
  and and_43 (and_43_out, EN, b2, a5);
  and and_44 (and_44_out, EN, b3, a5);
  and and_45 (and_45_out, EN, b4, a5);
  and and_46 (and_46_out, EN, b5, a5);
  and and_47 (and_47_out, EN, b6, a5);
  and and_48 (and_48_out, EN, b7, a5);
  and and_49 (and_49_out, EN, b0, a6);
  and and_50 (and_50_out, EN, b1, a6);
  and and_51 (and_51_out, EN, b2, a6);
  and and_52 (and_52_out, EN, b3, a6);
  and and_53 (and_53_out, EN, b4, a6);
  and and_54 (and_54_out, EN, b5, a6);
  and and_55 (and_55_out, EN, b6, a6);
  and and_56 (and_56_out, EN, b7, a6);
  and and_57 (and_57_out, EN, b0, a7);
  and and_58 (and_58_out, EN, b1, a7);
  and and_59 (and_59_out, EN, b2, a7);
  and and_60 (and_60_out, EN, b3, a7);
  and and_61 (and_61_out, EN, b4, a7);
  and and_62 (and_62_out, EN, b5, a7);
  and and_63 (and_63_out, EN, b6, a7);
  and and_64 (and_64_out, EN, b7, a7);
  _8_BitLookAhead u_8_bitlookahead_1 (
    .b7(and_58_out), .b6(and_50_out), .b5(and_42_out), .b3(and_26_out), .b4(and_34_out), .b2(and_18_out),
    .b1(and_10_out), .b0(and_2_out), .in_1(Zero), .o8(n8_bitlookahead_1_o8), .o7(n8_bitlookahead_1_o7),
    .o6(n8_bitlookahead_1_o6), .o5(n8_bitlookahead_1_o5), .o4(n8_bitlookahead_1_o4), .a7(Zero),
    .a6(and_57_out), .a5(and_49_out), .a3(and_33_out), .a4(and_41_out), .a2(and_25_out), .a1(and_17_out),
    .a0(and_9_out), .o3(n8_bitlookahead_1_o3), .o2(n8_bitlookahead_1_o2), .o1(n8_bitlookahead_1_o1), .o0(m1));
  _8_BitLookAhead u_8_bitlookahead_2 (
    .b7(and_60_out), .b6(and_52_out), .b5(and_44_out), .b3(and_28_out), .b4(and_36_out), .b2(and_20_out),
    .b1(and_12_out), .b0(and_4_out), .in_1(Zero), .o8(n8_bitlookahead_2_o8), .o7(n8_bitlookahead_2_o7),
    .o6(n8_bitlookahead_2_o6), .o5(n8_bitlookahead_2_o5), .o4(n8_bitlookahead_2_o4),
    .a7(n8_bitlookahead_6_o8), .a6(n8_bitlookahead_6_o7), .a5(n8_bitlookahead_6_o6),
    .a3(n8_bitlookahead_6_o4), .a4(n8_bitlookahead_6_o5), .a2(n8_bitlookahead_6_o3),
    .a1(n8_bitlookahead_6_o2), .a0(n8_bitlookahead_6_o1), .o3(n8_bitlookahead_2_o3),
    .o2(n8_bitlookahead_2_o2), .o1(n8_bitlookahead_2_o1), .o0(m3));
  _8_BitLookAhead u_8_bitlookahead_3 (
    .b7(and_61_out), .b6(and_53_out), .b5(and_45_out), .b3(and_29_out), .b4(and_37_out), .b2(and_21_out),
    .b1(and_13_out), .b0(and_5_out), .in_1(Zero), .o8(n8_bitlookahead_3_o8), .o7(n8_bitlookahead_3_o7),
    .o6(n8_bitlookahead_3_o6), .o5(n8_bitlookahead_3_o5), .o4(n8_bitlookahead_3_o4),
    .a7(n8_bitlookahead_2_o8), .a6(n8_bitlookahead_2_o7), .a5(n8_bitlookahead_2_o6),
    .a3(n8_bitlookahead_2_o4), .a4(n8_bitlookahead_2_o5), .a2(n8_bitlookahead_2_o3),
    .a1(n8_bitlookahead_2_o2), .a0(n8_bitlookahead_2_o1), .o3(n8_bitlookahead_3_o3),
    .o2(n8_bitlookahead_3_o2), .o1(n8_bitlookahead_3_o1), .o0(m4_prime));
  _8_BitLookAhead u_8_bitlookahead_4 (
    .b7(and_62_out), .b6(and_54_out), .b5(and_46_out), .b3(and_30_out), .b4(and_38_out), .b2(and_22_out),
    .b1(and_14_out), .b0(and_6_out), .in_1(Zero), .o8(n8_bitlookahead_4_o8), .o7(n8_bitlookahead_4_o7),
    .o6(n8_bitlookahead_4_o6), .o5(n8_bitlookahead_4_o5), .o4(n8_bitlookahead_4_o4),
    .a7(n8_bitlookahead_3_o8), .a6(n8_bitlookahead_3_o7), .a5(n8_bitlookahead_3_o6),
    .a3(n8_bitlookahead_3_o4), .a4(n8_bitlookahead_3_o5), .a2(n8_bitlookahead_3_o3),
    .a1(n8_bitlookahead_3_o2), .a0(n8_bitlookahead_3_o1), .o3(n8_bitlookahead_4_o3),
    .o2(n8_bitlookahead_4_o2), .o1(n8_bitlookahead_4_o1), .o0(m5));
  _8_BitLookAhead u_8_bitlookahead_5 (
    .b7(and_64_out), .b6(and_56_out), .b5(and_48_out), .b3(and_32_out), .b4(and_40_out), .b2(and_24_out),
    .b1(and_16_out), .b0(and_8_out), .in_1(Zero), .o8(m15), .o7(m14), .o6(m13), .o5(m12), .o4(m11),
    .a7(n8_bitlookahead_7_o8), .a6(n8_bitlookahead_7_o7), .a5(n8_bitlookahead_7_o6),
    .a3(n8_bitlookahead_7_o4), .a4(n8_bitlookahead_7_o5), .a2(n8_bitlookahead_7_o3),
    .a1(n8_bitlookahead_7_o2), .a0(n8_bitlookahead_7_o1), .o3(m10), .o2(m9), .o1(m8), .o0(m7));
  _8_BitLookAhead u_8_bitlookahead_6 (
    .b7(n8_bitlookahead_1_o8), .b6(n8_bitlookahead_1_o7), .b5(n8_bitlookahead_1_o6),
    .b3(n8_bitlookahead_1_o4), .b4(n8_bitlookahead_1_o5), .b2(n8_bitlookahead_1_o3),
    .b1(n8_bitlookahead_1_o2), .b0(n8_bitlookahead_1_o1), .in_1(Zero), .o8(n8_bitlookahead_6_o8),
    .o7(n8_bitlookahead_6_o7), .o6(n8_bitlookahead_6_o6), .o5(n8_bitlookahead_6_o5),
    .o4(n8_bitlookahead_6_o4), .a7(and_59_out), .a6(and_51_out), .a5(and_43_out), .a3(and_27_out),
    .a4(and_35_out), .a2(and_19_out), .a1(and_11_out), .a0(and_3_out), .o3(n8_bitlookahead_6_o3),
    .o2(n8_bitlookahead_6_o2), .o1(n8_bitlookahead_6_o1), .o0(m2));
  _8_BitLookAhead u_8_bitlookahead_7 (
    .b7(n8_bitlookahead_4_o8), .b6(n8_bitlookahead_4_o7), .b5(n8_bitlookahead_4_o6),
    .b3(n8_bitlookahead_4_o4), .b4(n8_bitlookahead_4_o5), .b2(n8_bitlookahead_4_o3),
    .b1(n8_bitlookahead_4_o2), .b0(n8_bitlookahead_4_o1), .in_1(Zero), .o8(n8_bitlookahead_7_o8),
    .o7(n8_bitlookahead_7_o7), .o6(n8_bitlookahead_7_o6), .o5(n8_bitlookahead_7_o5),
    .o4(n8_bitlookahead_7_o4), .a7(and_63_out), .a6(and_55_out), .a5(and_47_out), .a3(and_31_out),
    .a4(and_39_out), .a2(and_23_out), .a1(and_15_out), .a0(and_7_out), .o3(n8_bitlookahead_7_o3),
    .o2(n8_bitlookahead_7_o2), .o1(n8_bitlookahead_7_o1), .o0(m6));
endmodule

module Adder_Subtractor_8_Bit (
  input  a7,
  input  a6,
  input  a5,
  input  a4,
  input  a3,
  input  a2,
  input  a1,
  input  a0,
  input  a7_2,
  input  a6_2,
  input  a5_2,
  input  a4_2,
  input  a3_2,
  input  a2_2,
  input  a1_2,
  input  a0_2,
  input  M,
  input  O,
  output s0,
  output s1,
  output s2,
  output s3,
  output s4,
  output out_24,
  output s5,
  output s6,
  output s7,
  output s8
);

  wire n8_bitlookahead_1_o0, n8_bitlookahead_1_o1, n8_bitlookahead_1_o2, n8_bitlookahead_1_o3,
       n8_bitlookahead_1_o4, n8_bitlookahead_1_o5, n8_bitlookahead_1_o6, n8_bitlookahead_1_o7,
       n8_bitlookahead_1_o8, not_1_out, not_2_out, xor_1_out, xor_2_out, xor_3_out, xor_4_out, xor_5_out,
       xor_6_out, xor_7_out, xor_8_out;

  xor xor_1 (xor_1_out, M, a0_2);
  xor xor_2 (xor_2_out, M, a1_2);
  xor xor_3 (xor_3_out, a2_2, M);
  xor xor_4 (xor_4_out, a3_2, M);
  xor xor_5 (xor_5_out, a4_2, M);
  xor xor_6 (xor_6_out, a5_2, M);
  xor xor_7 (xor_7_out, a6_2, M);
  xor xor_8 (xor_8_out, a7_2, M);
  _8_BitLookAhead u_8_bitlookahead_1 (
    .b7(a7), .b6(a6), .b5(a5), .b3(a3), .b4(a4), .b2(a2), .b1(a1), .b0(a0), .in_1(M),
    .o8(n8_bitlookahead_1_o8), .o7(n8_bitlookahead_1_o7), .o6(n8_bitlookahead_1_o6),
    .o5(n8_bitlookahead_1_o5), .o4(n8_bitlookahead_1_o4), .a7(xor_8_out), .a6(xor_7_out), .a5(xor_6_out),
    .a3(xor_4_out), .a4(xor_5_out), .a2(xor_3_out), .a1(xor_2_out), .a0(xor_1_out),
    .o3(n8_bitlookahead_1_o3), .o2(n8_bitlookahead_1_o2), .o1(n8_bitlookahead_1_o1), .o0(n8_bitlookahead_1_o0));
  not not_1 (not_1_out, M);
  not not_2 (not_2_out, n8_bitlookahead_1_o8);
  and and_1 (s8, n8_bitlookahead_1_o8, not_1_out);
  and and_2 (out_24, M, not_2_out);
  _2_s_Compliment u_2_s_compliment_1 (
    .O(O), .S(out_24), .a7(n8_bitlookahead_1_o7), .a6(n8_bitlookahead_1_o6), .a5(n8_bitlookahead_1_o5),
    .a4(n8_bitlookahead_1_o4), .a3(n8_bitlookahead_1_o3), .a2(n8_bitlookahead_1_o2),
    .a1(n8_bitlookahead_1_o1), .a0(n8_bitlookahead_1_o0), .o0(s0), .o1(s1), .o2(s2), .o3(s3), .o4(s4),
    .o5(s5), .o6(s6), .o7(s7));
endmodule

module _2_s_Compliment (
  input  O,
  input  a7,
  input  a6,
  input  a5,
  input  a4,
  input  a3,
  input  a2,
  input  a1,
  input  a0,
  input  S,
  output o0,
  output o1,
  output o2,
  output o3,
  output o4,
  output o5,
  output o6,
  output o7
);

  wire multiplexer_1_out, multiplexer_2_out, multiplexer_3_out, multiplexer_4_out, multiplexer_5_out,
       multiplexer_6_out, multiplexer_7_out, multiplexer_8_out, not_1_out, not_2_out, not_3_out, not_4_out,
       not_5_out, not_6_out, not_7_out, not_8_out, not_9_out;

  not not_1 (not_1_out, a0);
  not not_2 (not_2_out, a1);
  not not_3 (not_3_out, a2);
  not not_4 (not_4_out, a3);
  not not_5 (not_5_out, a4);
  not not_6 (not_6_out, a5);
  not not_7 (not_7_out, a6);
  not not_8 (not_8_out, a7);
  Multiplexer multiplexer_1 (.in0(a0), .in1(not_1_out), .out(multiplexer_1_out), .sel(S), .en(O));
  Multiplexer multiplexer_2 (.in0(a1), .in1(not_2_out), .out(multiplexer_2_out), .sel(S), .en(O));
  Multiplexer multiplexer_3 (.in0(a2), .in1(not_3_out), .out(multiplexer_3_out), .sel(S), .en(O));
  Multiplexer multiplexer_4 (.in0(a3), .in1(not_4_out), .out(multiplexer_4_out), .sel(S), .en(O));
  Multiplexer multiplexer_5 (.in0(a4), .in1(not_5_out), .out(multiplexer_5_out), .sel(S), .en(O));
  Multiplexer multiplexer_6 (.in0(a5), .in1(not_6_out), .out(multiplexer_6_out), .sel(S), .en(O));
  Multiplexer multiplexer_7 (.in0(a6), .in1(not_7_out), .out(multiplexer_7_out), .sel(S), .en(O));
  Multiplexer multiplexer_8 (.in0(a7), .in1(not_8_out), .out(multiplexer_8_out), .sel(S), .en(O));
  not not_9 (not_9_out, O);
  _8_BitLookAhead u_8_bitlookahead_1 (
    .b7(multiplexer_8_out), .b6(multiplexer_7_out), .b5(multiplexer_6_out), .b3(multiplexer_4_out),
    .b4(multiplexer_5_out), .b2(multiplexer_3_out), .b1(multiplexer_2_out), .b0(multiplexer_1_out),
    .in_1(not_9_out), .o7(o7), .o6(o6), .o5(o5), .o4(o4), .a7(not_9_out), .a6(not_9_out), .a5(not_9_out),
    .a3(not_9_out), .a4(not_9_out), .a2(not_9_out), .a1(not_9_out), .a0(S), .o3(o3), .o2(o2), .o1(o1), .o0(o0));  // open: o8
endmodule

module hexato7segment (
  input  a0,
  input  a1,
  input  a2,
  input  a3,
  output a,
  output b,
  output c,
  output d,
  output e,
  output f,
  output g
);

  wire decoder_1_out0, decoder_1_out1, decoder_1_out2, decoder_1_out3, decoder_1_out4, decoder_1_out5,
       decoder_1_out6, decoder_1_out7, decoder_1_out8, decoder_1_out9, decoder_1_out10, decoder_1_out11,
       decoder_1_out12, decoder_1_out13, decoder_1_out14, decoder_1_out15;

  Decoder #(.select(4)) decoder_1 (
    .out0(decoder_1_out0), .out1(decoder_1_out1), .out2(decoder_1_out2), .out3(decoder_1_out3),
    .out4(decoder_1_out4), .out5(decoder_1_out5), .out6(decoder_1_out6), .out7(decoder_1_out7),
    .out8(decoder_1_out8), .out9(decoder_1_out9), .out10(decoder_1_out10), .out11(decoder_1_out11),
    .out12(decoder_1_out12), .out13(decoder_1_out13), .out14(decoder_1_out14), .out15(decoder_1_out15),
    .sel({a3, a2, a1, a0}), .en(1'b1));
  or u_a (a, decoder_1_out0, decoder_1_out1, decoder_1_out2, decoder_1_out3, decoder_1_out4, decoder_1_out7, decoder_1_out8, decoder_1_out9, decoder_1_out10, decoder_1_out13);
  or u_b (b, decoder_1_out0, decoder_1_out1, decoder_1_out3, decoder_1_out4, decoder_1_out5, decoder_1_out6, decoder_1_out7, decoder_1_out8, decoder_1_out9, decoder_1_out10, decoder_1_out11, decoder_1_out13);
  or u_c (c, decoder_1_out0, decoder_1_out2, decoder_1_out3, decoder_1_out5, decoder_1_out6, decoder_1_out8, decoder_1_out11, decoder_1_out12, decoder_1_out13, decoder_1_out14);
  or u_d (d, decoder_1_out0, decoder_1_out2, decoder_1_out6, decoder_1_out8, decoder_1_out10, decoder_1_out11, decoder_1_out12, decoder_1_out13, decoder_1_out14, decoder_1_out15);
  or u_e (e, decoder_1_out0, decoder_1_out4, decoder_1_out5, decoder_1_out6, decoder_1_out8, decoder_1_out9, decoder_1_out10, decoder_1_out11, decoder_1_out12, decoder_1_out14, decoder_1_out15);
  or u_f (f, decoder_1_out0, decoder_1_out2, decoder_1_out3, decoder_1_out5, decoder_1_out6, decoder_1_out7, decoder_1_out8, decoder_1_out9, decoder_1_out10, decoder_1_out12, decoder_1_out14, decoder_1_out15);
  or u_g (g, decoder_1_out2, decoder_1_out3, decoder_1_out4, decoder_1_out5, decoder_1_out6, decoder_1_out8, decoder_1_out9, decoder_1_out10, decoder_1_out11, decoder_1_out13, decoder_1_out14, decoder_1_out15);
endmodule

module _16orgates (
  input  a0,
  input  b0,
  input  a0_2,
  input  b0_2,
  input  a0_3,
  input  b0_3,
  input  a0_4,
  input  b0_4,
  input  a0_5,
  input  b0_5,
  input  a0_6,
  input  b0_6,
  input  a0_7,
  input  b0_7,
  input  a0_8,
  input  b0_8,
  input  a0_9,
  input  b0_9,
  input  a0_10,
  input  b0_10,
  input  a0_11,
  input  b0_11,
  input  a0_12,
  input  b0_12,
  input  a0_13,
  input  b0_13,
  input  a0_14,
  input  b0_14,
  input  a0_15,
  input  b0_15,
  input  a0_16,
  input  b0_16,
  output out_33,
  output out_34,
  output out_35,
  output out_36,
  output out_37,
  output out_38,
  output out_39,
  output out_40,
  output out_41,
  output out_42,
  output out_43,
  output out_44,
  output out_45,
  output out_46,
  output out_47,
  output out_48
);

  or or_1 (out_33, a0, b0);
  or or_2 (out_34, a0_2, b0_2);
  or or_3 (out_35, a0_3, b0_3);
  or or_4 (out_36, a0_4, b0_4);
  or or_5 (out_37, a0_5, b0_5);
  or or_6 (out_38, a0_6, b0_6);
  or or_7 (out_39, a0_7, b0_7);
  or or_8 (out_40, a0_8, b0_8);
  or or_9 (out_41, a0_9, b0_9);
  or or_10 (out_42, a0_10, b0_10);
  or or_11 (out_43, a0_11, b0_11);
  or or_12 (out_44, a0_12, b0_12);
  or or_13 (out_45, a0_13, b0_13);
  or or_14 (out_46, a0_14, b0_14);
  or or_15 (out_47, a0_15, b0_15);
  or or_16 (out_48, a0_16, b0_16);
endmodule

module _9andgates (
  input  EN,
  input  a0,
  input  a1,
  input  a2,
  input  a3,
  input  a4,
  input  a5,
  input  a6,
  input  a7,
  input  a8,
  output out_11,
  output out_12,
  output out_13,
  output out_14,
  output out_15,
  output out_16,
  output out_17,
  output out_18,
  output out_19
);

  and and_1 (out_11, a0, EN);
  and and_2 (out_12, a1, EN);
  and and_3 (out_13, a2, EN);
  and and_4 (out_14, a3, EN);
  and and_5 (out_15, a4, EN);
  and and_6 (out_16, a5, EN);
  and and_7 (out_17, a6, EN);
  and and_8 (out_18, a7, EN);
  and and_9 (out_19, a8, EN);
endmodule

module restorelogic (
  input  in_1,
  input  in_2,
  input  in_3,
  input  in_4,
  input  in_5,
  input  in_6,
  input  in_7,
  input  in_8,
  input  in_9,
  input  in_10,
  input  in_11,
  input  in_12,
  input  in_13,
  input  in_14,
  input  in_15,
  input  in_16,
  input  in_17,
  output out_18,
  output out_19,
  output out_20,
  output out_21,
  output out_22,
  output out_23,
  output out_24,
  output out_25
);

  wire not_1_out;

  not not_1 (not_1_out, in_17);
  Multiplexer multiplexer_1 (.in0(in_9), .in1(in_1), .out(out_18), .sel(not_1_out), .en(1'b1));
  Multiplexer multiplexer_2 (.in0(in_10), .in1(in_2), .out(out_19), .sel(not_1_out), .en(1'b1));
  Multiplexer multiplexer_3 (.in0(in_11), .in1(in_3), .out(out_20), .sel(not_1_out), .en(1'b1));
  Multiplexer multiplexer_4 (.in0(in_12), .in1(in_4), .out(out_21), .sel(not_1_out), .en(1'b1));
  Multiplexer multiplexer_5 (.in0(in_13), .in1(in_5), .out(out_22), .sel(not_1_out), .en(1'b1));
  Multiplexer multiplexer_6 (.in0(in_15), .in1(in_7), .out(out_24), .sel(not_1_out), .en(1'b1));
  Multiplexer multiplexer_7 (.in0(in_14), .in1(in_6), .out(out_23), .sel(not_1_out), .en(1'b1));
  Multiplexer multiplexer_8 (.in0(in_16), .in1(in_8), .out(out_25), .sel(not_1_out), .en(1'b1));
endmodule

module dividorcelleach (
  input  a7,
  input  a6,
  input  a5,
  input  a5_2,
  input  a5_3,
  input  a5_4,
  input  a5_5,
  input  a5_6,
  input  a7_2,
  input  a6_2,
  input  a5_7,
  input  a5_8,
  input  a5_9,
  input  a5_10,
  input  a5_11,
  input  a5_12,
  output out_17,
  output LSB,
  output out_19,
  output out_20,
  output out_21,
  output out_22,
  output out_23,
  output out_24,
  output out_25
);

  wire adder_subtractor_8_bit_1_s0, adder_subtractor_8_bit_1_s1, adder_subtractor_8_bit_1_s2,
       adder_subtractor_8_bit_1_s3, adder_subtractor_8_bit_1_s4, adder_subtractor_8_bit_1_s5,
       adder_subtractor_8_bit_1_s6, adder_subtractor_8_bit_1_s7;

  restorelogic restorelogic_1 (
    .in_17(out_17), .in_9(a7), .in_10(a6), .in_11(a5), .in_12(a5_2), .in_13(a5_3), .in_14(a5_4),
    .in_15(a5_5), .in_16(a5_6), .in_1(adder_subtractor_8_bit_1_s7), .in_2(adder_subtractor_8_bit_1_s6),
    .in_3(adder_subtractor_8_bit_1_s5), .in_4(adder_subtractor_8_bit_1_s4),
    .in_5(adder_subtractor_8_bit_1_s3), .in_6(adder_subtractor_8_bit_1_s2),
    .in_7(adder_subtractor_8_bit_1_s1), .in_8(adder_subtractor_8_bit_1_s0), .out_18(out_25), .out_19(out_24),
    .out_20(out_23), .out_21(out_22), .out_22(out_21), .out_23(out_20), .out_24(out_19), .out_25(LSB));
  Adder_Subtractor_8_Bit adder_subtractor_8_bit_1 (
    .a7(a7), .a6(a6), .a5(a5), .a4(a5_2), .a3(a5_3), .a2(a5_4), .a1(a5_5), .a0(a5_6), .a7_2(a7_2),
    .a6_2(a6_2), .a5_2(a5_7), .a4_2(a5_8), .a3_2(a5_9), .a2_2(a5_10), .a1_2(a5_11), .a0_2(a5_12), .M(1'b1),
    .s0(adder_subtractor_8_bit_1_s0), .s1(adder_subtractor_8_bit_1_s1), .s2(adder_subtractor_8_bit_1_s2),
    .s3(adder_subtractor_8_bit_1_s3), .s4(adder_subtractor_8_bit_1_s4), .s5(adder_subtractor_8_bit_1_s5),
    .s6(adder_subtractor_8_bit_1_s6), .s7(adder_subtractor_8_bit_1_s7), .O(1'b1), .out_24(out_17));  // open: s8
endmodule

module dividor8bit (
  input  a7,
  input  a6,
  input  a5,
  input  a4,
  input  a3,
  input  a2,
  input  a1,
  input  a0,
  input  b7,
  input  b6,
  input  b5,
  input  b4,
  input  b3,
  input  b2,
  input  b1,
  input  b0,
  output out_17,
  output q6,
  output q5,
  output q4,
  output q3,
  output out_22,
  output out_23,
  output out_24,
  output out_25,
  output out_26,
  output out_27,
  output out_28,
  output out_29,
  output r2,
  output r1,
  output LSB
);

  wire dividorcelleach_1_lsb, dividorcelleach_1_out_17, dividorcelleach_1_out_19, dividorcelleach_1_out_20,
       dividorcelleach_1_out_21, dividorcelleach_1_out_22, dividorcelleach_1_out_23,
       dividorcelleach_1_out_24, dividorcelleach_2_lsb, dividorcelleach_2_out_17, dividorcelleach_2_out_19,
       dividorcelleach_2_out_20, dividorcelleach_2_out_21, dividorcelleach_2_out_22,
       dividorcelleach_2_out_23, dividorcelleach_2_out_24, dividorcelleach_3_lsb, dividorcelleach_3_out_17,
       dividorcelleach_3_out_19, dividorcelleach_3_out_20, dividorcelleach_3_out_21,
       dividorcelleach_3_out_22, dividorcelleach_3_out_23, dividorcelleach_3_out_24, dividorcelleach_4_lsb,
       dividorcelleach_4_out_17, dividorcelleach_4_out_19, dividorcelleach_4_out_20,
       dividorcelleach_4_out_21, dividorcelleach_4_out_22, dividorcelleach_4_out_23,
       dividorcelleach_4_out_24, dividorcelleach_5_lsb, dividorcelleach_5_out_17, dividorcelleach_5_out_19,
       dividorcelleach_5_out_20, dividorcelleach_5_out_21, dividorcelleach_5_out_22,
       dividorcelleach_5_out_23, dividorcelleach_5_out_24, dividorcelleach_6_lsb, dividorcelleach_6_out_17,
       dividorcelleach_6_out_19, dividorcelleach_6_out_20, dividorcelleach_6_out_21,
       dividorcelleach_6_out_22, dividorcelleach_6_out_23, dividorcelleach_6_out_24, dividorcelleach_7_lsb,
       dividorcelleach_7_out_17, dividorcelleach_7_out_19, dividorcelleach_7_out_20,
       dividorcelleach_7_out_21, dividorcelleach_7_out_22, dividorcelleach_7_out_23,
       dividorcelleach_7_out_24, dividorcelleach_8_out_17;

  dividorcelleach dividorcelleach_1 (
    .LSB(dividorcelleach_1_lsb), .out_19(dividorcelleach_1_out_19), .out_20(dividorcelleach_1_out_20),
    .out_21(dividorcelleach_1_out_21), .out_22(dividorcelleach_1_out_22), .out_23(dividorcelleach_1_out_23),
    .out_24(dividorcelleach_1_out_24), .a7(1'b0), .a6(1'b0), .a5(1'b0), .a5_2(1'b0), .a5_3(1'b0),
    .a5_4(1'b0), .a5_5(1'b0), .a5_6(a7), .a7_2(b7), .a6_2(b6), .a5_7(b5), .a5_8(b4), .a5_9(b3), .a5_10(b2),
    .a5_11(b1), .a5_12(b0), .out_17(dividorcelleach_1_out_17));  // open: out_25
  dividorcelleach dividorcelleach_2 (
    .LSB(dividorcelleach_2_lsb), .out_19(dividorcelleach_2_out_19), .out_20(dividorcelleach_2_out_20),
    .out_21(dividorcelleach_2_out_21), .out_22(dividorcelleach_2_out_22), .out_23(dividorcelleach_2_out_23),
    .out_24(dividorcelleach_2_out_24), .a7(dividorcelleach_1_out_24), .a6(dividorcelleach_1_out_23),
    .a5(dividorcelleach_1_out_22), .a5_2(dividorcelleach_1_out_21), .a5_3(dividorcelleach_1_out_20),
    .a5_4(dividorcelleach_1_out_19), .a5_5(dividorcelleach_1_lsb), .a5_6(a6), .a7_2(b7), .a6_2(b6),
    .a5_7(b5), .a5_8(b4), .a5_9(b3), .a5_10(b2), .a5_11(b1), .a5_12(b0), .out_17(dividorcelleach_2_out_17));  // open: out_25
  dividorcelleach dividorcelleach_3 (
    .LSB(dividorcelleach_3_lsb), .out_19(dividorcelleach_3_out_19), .out_20(dividorcelleach_3_out_20),
    .out_21(dividorcelleach_3_out_21), .out_22(dividorcelleach_3_out_22), .out_23(dividorcelleach_3_out_23),
    .out_24(dividorcelleach_3_out_24), .a7(dividorcelleach_2_out_24), .a6(dividorcelleach_2_out_23),
    .a5(dividorcelleach_2_out_22), .a5_2(dividorcelleach_2_out_21), .a5_3(dividorcelleach_2_out_20),
    .a5_4(dividorcelleach_2_out_19), .a5_5(dividorcelleach_2_lsb), .a5_6(a5), .a7_2(b7), .a6_2(b6),
    .a5_7(b5), .a5_8(b4), .a5_9(b3), .a5_10(b2), .a5_11(b1), .a5_12(b0), .out_17(dividorcelleach_3_out_17));  // open: out_25
  dividorcelleach dividorcelleach_4 (
    .LSB(dividorcelleach_4_lsb), .out_19(dividorcelleach_4_out_19), .out_20(dividorcelleach_4_out_20),
    .out_21(dividorcelleach_4_out_21), .out_22(dividorcelleach_4_out_22), .out_23(dividorcelleach_4_out_23),
    .out_24(dividorcelleach_4_out_24), .a7(dividorcelleach_3_out_24), .a6(dividorcelleach_3_out_23),
    .a5(dividorcelleach_3_out_22), .a5_2(dividorcelleach_3_out_21), .a5_3(dividorcelleach_3_out_20),
    .a5_4(dividorcelleach_3_out_19), .a5_5(dividorcelleach_3_lsb), .a5_6(a4), .a7_2(b7), .a6_2(b6),
    .a5_7(b5), .a5_8(b4), .a5_9(b3), .a5_10(b2), .a5_11(b1), .a5_12(b0), .out_17(dividorcelleach_4_out_17));  // open: out_25
  dividorcelleach dividorcelleach_5 (
    .LSB(dividorcelleach_5_lsb), .out_19(dividorcelleach_5_out_19), .out_20(dividorcelleach_5_out_20),
    .out_21(dividorcelleach_5_out_21), .out_22(dividorcelleach_5_out_22), .out_23(dividorcelleach_5_out_23),
    .out_24(dividorcelleach_5_out_24), .a7(dividorcelleach_4_out_24), .a6(dividorcelleach_4_out_23),
    .a5(dividorcelleach_4_out_22), .a5_2(dividorcelleach_4_out_21), .a5_3(dividorcelleach_4_out_20),
    .a5_4(dividorcelleach_4_out_19), .a5_5(dividorcelleach_4_lsb), .a5_6(a3), .a7_2(b7), .a6_2(b6),
    .a5_7(b5), .a5_8(b4), .a5_9(b3), .a5_10(b2), .a5_11(b1), .a5_12(b0), .out_17(dividorcelleach_5_out_17));  // open: out_25
  dividorcelleach dividorcelleach_6 (
    .LSB(dividorcelleach_6_lsb), .out_19(dividorcelleach_6_out_19), .out_20(dividorcelleach_6_out_20),
    .out_21(dividorcelleach_6_out_21), .out_22(dividorcelleach_6_out_22), .out_23(dividorcelleach_6_out_23),
    .out_24(dividorcelleach_6_out_24), .a7(dividorcelleach_5_out_24), .a6(dividorcelleach_5_out_23),
    .a5(dividorcelleach_5_out_22), .a5_2(dividorcelleach_5_out_21), .a5_3(dividorcelleach_5_out_20),
    .a5_4(dividorcelleach_5_out_19), .a5_5(dividorcelleach_5_lsb), .a5_6(a2), .a7_2(b7), .a6_2(b6),
    .a5_7(b5), .a5_8(b4), .a5_9(b3), .a5_10(b2), .a5_11(b1), .a5_12(b0), .out_17(dividorcelleach_6_out_17));  // open: out_25
  dividorcelleach dividorcelleach_7 (
    .LSB(dividorcelleach_7_lsb), .out_19(dividorcelleach_7_out_19), .out_20(dividorcelleach_7_out_20),
    .out_21(dividorcelleach_7_out_21), .out_22(dividorcelleach_7_out_22), .out_23(dividorcelleach_7_out_23),
    .out_24(dividorcelleach_7_out_24), .a7(dividorcelleach_6_out_24), .a6(dividorcelleach_6_out_23),
    .a5(dividorcelleach_6_out_22), .a5_2(dividorcelleach_6_out_21), .a5_3(dividorcelleach_6_out_20),
    .a5_4(dividorcelleach_6_out_19), .a5_5(dividorcelleach_6_lsb), .a5_6(a1), .a7_2(b7), .a6_2(b6),
    .a5_7(b5), .a5_8(b4), .a5_9(b3), .a5_10(b2), .a5_11(b1), .a5_12(b0), .out_17(dividorcelleach_7_out_17));  // open: out_25
  not not_1 (out_17, dividorcelleach_1_out_17);
  not not_2 (q6, dividorcelleach_2_out_17);
  not not_3 (q5, dividorcelleach_3_out_17);
  not not_4 (q4, dividorcelleach_4_out_17);
  not not_5 (q3, dividorcelleach_5_out_17);
  dividorcelleach dividorcelleach_8 (
    .LSB(LSB), .out_19(r1), .out_20(r2), .out_21(out_29), .out_22(out_28), .out_23(out_27), .out_24(out_26),
    .out_25(out_25), .a7(dividorcelleach_7_out_24), .a6(dividorcelleach_7_out_23),
    .a5(dividorcelleach_7_out_22), .a5_2(dividorcelleach_7_out_21), .a5_3(dividorcelleach_7_out_20),
    .a5_4(dividorcelleach_7_out_19), .a5_5(dividorcelleach_7_lsb), .a5_6(a0), .a7_2(b7), .a6_2(b6),
    .a5_7(b5), .a5_8(b4), .a5_9(b3), .a5_10(b2), .a5_11(b1), .a5_12(b0), .out_17(dividorcelleach_8_out_17));
  not not_6 (out_22, dividorcelleach_6_out_17);
  not not_7 (out_23, dividorcelleach_7_out_17);
  not not_8 (out_24, dividorcelleach_8_out_17);
endmodule
